# Fritzing sketch sketch (saved by Fritzing 0.9.3b)
breadboards: 1

parts:
  Part1 = Arduino Uno (Rev3)
  R1 = Resistor [tolerance=±5% resistance=220 package=THT]
  Part2 = Bluetooth HC-05 Macho
  LED1 = smd LED [color="Red (633nm)" package="0603 [SMD]"]
  RHT1 = Humidity and Temperature Sensor RHT03

nets:
  N1: Part1.D9_PWM, RHT1.Data-signal
  N2: Part1.D13/SCK, R1.Pin_1
  N3: Part1.D0/RX, Part2.TXD
  N4: Part1.D1/TX, Part2.RXD
  VCC: Part1.5V, Part2.VCC, RHT1.Vcc
  GND: Part1.GND, Part2.GND, LED1.cathode, RHT1.GND_1
  N5: R1.Pin_0, LED1.anode
